# Fritzing sketch Temperature-Station (saved by Fritzing 0.9.3b)
circuit board: 5.03873cm x 8.96154cm
breadboards: 1

parts:
  J1 = female pin header, 15 pins [form="♀ (female)"]
  J2 = female pin header, 15 pins [form="♀ (female)"]
  U1 = V_REG_LD1117VXX [part_number=LD33V3 package=78xxl]
  R1 = Resistor [tolerance=±5% resistance=4.7k package=THT]
  R2 = Resistor [tolerance=±5% resistance=4.7k package=THT]
  R1_R2_R3 = Resistor [tolerance=±5% resistance=4.7k package=THT]
  -/+ = female pin header, 2 pins [form="♀ (female)"]
  C1 = Electrolytic Capacitor [capacitance=10µF voltage=10V package="100 mil [THT, electrolytic]"]
  C3 = Electrolytic Capacitor [capacitance=10µF voltage=10V package="100 mil [THT, electrolytic]"]
  C4 = Ceramic Capacitor [capacitance=100nF voltage=10V package="200 mil [THT, multilayer]"]
  C2 = Ceramic Capacitor [capacitance=100nF voltage=10V package="200 mil [THT, multilayer]"]
  SD = double row female pin header, 16 pins [form="♀ (female)"]
  DS3231 = female pin header, 4 pins [form="♀ (female)"]
  J4 = female pin header, 3 pins [form="♀ (female)"]
  J3 = female pin header, 3 pins [form="♀ (female)"]
  J6 = female pin header, 3 pins [form="♀ (female)"]
  J5 = female pin header, 3 pins [form="♀ (female)"]

nets:
  N1: J1.pin2, J1.pin6, J2.pin2, J2.pin9, U1.GND, -/+.pin1, C1.-, C3.-, C4.0, C2.0, SD.pin1, SD.pin8, SD.pin9, SD.pin16, DS3231.pin1, J4.pin1, J3.pin1, J6.pin1, J5.pin1
  N2: J1.pin5, J2.pin1, J2.pin10, U1.OUT, R1.Pin_1, R2.Pin_1, R1_R2_R3.Pin_1, C1.+, C4.1, SD.pin2, SD.pin15, DS3231.pin2, J4.pin3, J3.pin3, J6.pin3, J5.pin3
  N3: J2.pin6, SD.pin5, SD.pin12
  N4: J2.pin7, SD.pin7, SD.pin10
  N5: J2.pin8, SD.pin6, SD.pin11
  N6: J2.pin11, SD.pin4, SD.pin13
  N7: J2.pin12, R1.Pin_0, J4.pin2, J3.pin2, J6.pin2, J5.pin2
  N8: J2.pin13, R1_R2_R3.Pin_0, DS3231.pin4
  N9: J2.pin14, R2.Pin_0, DS3231.pin3
  N10: U1.IN, -/+.pin2, C3.+, C2.1
  N11: SD.pin3, SD.pin14

notes:
  GND/3V3/5V/CS/MO/SCK/MI/GND
  GND/Vcc/SDA/SCL
  -/DATA/+
  NodeMCU 1.0
  USB
  Serwer Temperatur
  Marek Ledworowski
